# Fritzing sketch RGB display_v4 (saved by Fritzing 1.0.7)
circuit board: 6.35906cm x 4.86149cm
breadboards: 1

parts:
  5V_GND = JST XH 2A male [form="♂ (male)" package=THT]
  GND_D_5V = female pin header, 3 pins [form="♀ (female)"]
  PWR3 = female pin header, 2 pins [form="♀ (female)"]
  PWR4 = female pin header, 2 pins [form="♀ (female)"]
  PWR2 = female pin header, 2 pins [form="♀ (female)"]
  PWR1 = female pin header, 2 pins [form="♀ (female)"]
  R1 = Resistor [tolerance=±5% power=0.25W resistance=330 package=THT]
  C2 = Capacitor [package=cap-pth-5mm]
  C3 = Capacitor [package=cap-pth-5mm]
  C4 = Capacitor [package=cap-pth-5mm]
  C5 = Capacitor [package=cap-pth-5mm]
  C6 = Capacitor [package=cap-pth-5mm]
  74AHCT125 = 74AHCT125 [part_number=SN74AHCT125 package=dil14]
  C1 = Capacitor Polarized [package=cpol-radial-100uf-25v]
  ESP32-S3-N16R8 = female pin header, 22 pins [form="♀ (female)"]
  ESP32-S3-N16R9 = female pin header, 22 pins [form="♀ (female)"]  # not connected
  GND_SDA_SCL_5V = female pin header, 4 pins [form="♀ (female)"]

nets:
  N1: 5V_GND.pin1, GND_D_5V.pin3, PWR3.pin1, PWR4.pin1, PWR2.pin1, PWR1.pin1, C2.1, C3.1, C4.1, C5.1, C6.2, 74AHCT125.2OE, 74AHCT125.3OE, 74AHCT125.4OE, 74AHCT125.VCC, C1.+, ESP32-S3-N16R8.pin21, GND_SDA_SCL_5V.pin4
  N2: GND_D_5V.pin2, R1.Pin_0
  N3: R1.Pin_1, 74AHCT125.1Y
  N4: 74AHCT125.1A, ESP32-S3-N16R8.pin9
  N5: ESP32-S3-N16R8.pin12, GND_SDA_SCL_5V.pin2
  N6: ESP32-S3-N16R8.pin15, GND_SDA_SCL_5V.pin3

notes:
  G.C. - 2026

custom parts:
  JST XH 2A male: JST XH-2A
  74AHCT125: Quad Level-Shifter (3V to 5V) Quadruple Bus Buffer Gates With 3-State Outputs
